# Fritzing sketch RGB_LED_01 (saved by Fritzing 0.9.3b)
circuit board: 6.88566cm x 5.36311cm
breadboards: 1

parts:
  R4 = Resistor [resistance=220 tolerance=±5% package=THT]
  R5 = Resistor [resistance=220 tolerance=±5% package=THT]
  R6 = Resistor [resistance=220 tolerance=±5% package=THT]
  Arduino1 = Arduino Uno (Rev3)
  LED = RGB LED - (4 legs) [package="5 mm [THT]"]

nets:
  N1: R4.Pin_0, Arduino1.D11_PWM/MOSI
  N2: R4.Pin_1, LED.red_cathode
  N3: R5.Pin_0, Arduino1.D9_PWM
  N4: R5.Pin_1, LED.blue_cathode
  N5: R6.Pin_0, Arduino1.D10_PWM/SS
  N6: R6.Pin_1, LED.green_cathode
  N7: Arduino1.5V, LED.common_anode
