# Fritzing sketch RGB_LED_03 (saved by Fritzing 0.9.3b)
circuit board: 6.88566cm x 5.36311cm
breadboards: 1

parts:
  R4 = Resistor [resistance=220 tolerance=±5% package=THT]
  R5 = Resistor [resistance=220 tolerance=±5% package=THT]
  R6 = Resistor [resistance=220 tolerance=±5% package=THT]
  Arduino1 = Arduino Uno (Rev3)
  LED = RGB LED - (4 legs) [package="5 mm [THT]"]
  R7 = Rotary Potentiometer (Small) [maximum_resistance=10kΩ package=THT]
  R8 = Rotary Potentiometer (Small) [maximum_resistance=10kΩ package=THT]
  R9 = Rotary Potentiometer (Small) [maximum_resistance=10kΩ package=THT]

nets:
  N1: R4.Pin_0, Arduino1.D11_PWM/MOSI
  N2: R4.Pin_1, LED.red_cathode
  N3: R5.Pin_0, Arduino1.D9_PWM
  N4: R5.Pin_1, LED.blue_cathode
  N5: R6.Pin_0, Arduino1.D10_PWM/SS
  N6: R6.Pin_1, LED.green_cathode
  N7: Arduino1.A0, R7.wiper
  N8: Arduino1.A1, R8.wiper
  N9: Arduino1.A2, R9.wiper
  N10: Arduino1.GND, R7.leg1, R8.leg1, R9.leg1
  N11: Arduino1.5V, LED.common_anode, R7.leg2, R8.leg2, R9.leg2
